# Fritzing sketch board-schematic-v1 (saved by Fritzing 0.9.4)
breadboards: 1

parts:
  Raspberry_Pi_1 = Raspberry Pi 3 [part_number=RPI-3-V1.2]
  Part1 = QuadStepper
  M1 = DC Motor
  M2 = DC Motor
  M4 = DC Motor
  M3 = DC Motor

nets:
  N1: Raspberry_Pi_1.GIPO19, Part1.RST2
  N2: Raspberry_Pi_1.GIPO26, Part1.RST1
  N3: Raspberry_Pi_1.GIPO21, Part1.MS11
  N4: Raspberry_Pi_1.GIPO20, Part1.MS12
  N5: Raspberry_Pi_1.GIPO16, Part1.MS21
  GND: Raspberry_Pi_1.GND
  N6: Raspberry_Pi_1.GIPO12, Part1.MS22
  N7: Raspberry_Pi_1.GIPO25, Part1.MS31
  N8: Raspberry_Pi_1.GIPO24, Part1.MS32
  5V: Raspberry_Pi_1.5V
  N9: Part1.1-1B, M1.pin_2
  N10: Part1.1-1A, M1.pin_1
  12V: Part1.VOUT
  N11: Part1.3-1B, M3.pin_2
  N12: Part1.3-1A, M3.pin_1
  N13: Part1.4-1B, M4.pin_2
  N14: Part1.4-1A, M4.pin_1
  N15: Part1.2-1B, M2.pin_2
  N16: Part1.2-1A, M2.pin_1
